# Fritzing sketch Poseiduino-v0_1-mosfet (saved by Fritzing 0.9.2b)
stripboards: 3

parts:
  J1 = Basic Servo
  Bauteil2 = Arduino Nano (Rev3.0)
  VCC2 = Battery block 9V
  Q2 = Basic FET N-Channel [package="D2Pak [SMD]"]
  D2 = Rectifier Diode [part_number=1N4001 package="300 mil [THT]"]
  M2 = DC Motor
  R4 = Resistor [tolerance=±5% resistance=10k package=THT]
  R5 = Resistor [tolerance=±5% resistance=10k package="1206 [SMD]"]
  LED2 = smd LED [color="White (4500K)" package="1206 [SMD]"]

nets:
  GND: J1.gnd, Bauteil2.GND, VCC2.-, Q2.source, R4.Pin_1, R5.Pin_0
  VCC: J1.vcc, Bauteil2.5V, LED2.anode
  N1: J1.pulse, Bauteil2.D5
  N2: Bauteil2.D3, Q2.Gate, R4.Pin_0
  N3: VCC2.+, D2.cathode, M2.pin_1
  N4: Q2.drain, D2.anode, M2.pin_2
  N5: R5.Pin_1, LED2.cathode
